# Fritzing sketch circuit (saved by Fritzing 0.9.4)
breadboards: 1

parts:
  R5 = Resistor [tolerance=±5% resistance=10k package=THT]
  元件1 = Arduino Uno (Rev3) - ICSP
  C1 = Ceramic Capacitor [capacitance=100nF package="100 mil [THT, multilayer]"]

nets:
  N1: R5.Pin_0, 元件1.GND
  N2: R5.Pin_1, 元件1.A0, C1.1
  N3: 元件1.5V, C1.0
